// Logisim project 1400 ARITHMATIC LOGIC UNIT PROJECT.circ as structural Verilog: 1 circuit, main circuit main
module main (
  input  A,
  input  CARRY_IN,
  input  B,
  input  in_4,
  input  [1:0] OPERATION,
  input  in_6,
  output OUTPUT,
  output CARRY_OUT
);

  wire adder_1_out, and_1_out, multiplexer_1_out, multiplexer_2_out, not_1_out, not_2_out, or_1_out;

  not not_1 (not_1_out, A);
  not not_2 (not_2_out, B);
  Multiplexer multiplexer_1 (.in0(not_1_out), .in1(A), .out(multiplexer_1_out), .sel(in_4));  // open: en
  Multiplexer multiplexer_2 (.in0(not_2_out), .in1(B), .out(multiplexer_2_out), .sel(in_6));  // open: en
  and and_1 (and_1_out, multiplexer_1_out, multiplexer_2_out);
  or or_1 (or_1_out, multiplexer_1_out, multiplexer_2_out);
  Adder #(.width(1)) adder_1 (
    .a(multiplexer_1_out), .b(multiplexer_2_out), .out(adder_1_out), .cin(CARRY_IN), .cout(CARRY_OUT));
  Multiplexer #(.select(2)) multiplexer_3 (
    .in0(and_1_out), .in1(or_1_out), .in2(adder_1_out), .out(OUTPUT), .sel(OPERATION));  // open: in3, en
endmodule
